# Fritzing sketch Schets1 (saved by Fritzing 0.9.3b)
breadboards: 1

parts:
  Micro-controller = Electron
  SD-Logger = OpenLog
  R1 = Temperature Sensor (Thermistor) [thermistor_type=NTC package=THT]
  R = Resistor [tolerance=±5% resistance=10k package="2512 [SMD]"]
  Parking_sensor = hc-sr04

nets (from the schematic view):
  N1: Micro-controller.A2, R1.pin_0, R.Pin_1
  N2: Micro-controller.A3, Parking_sensor.Echo
  N3: Micro-controller.RX, SD-Logger.TXO
  N4: Micro-controller.TX, SD-Logger.RXI
  GND: Micro-controller.GND, SD-Logger.GND, R.Pin_0, Parking_sensor.GND
  N5: Micro-controller.VIN, Micro-controller.B0, Parking_sensor.Trig
  3V3: Micro-controller.3V3, SD-Logger.VCC, R1.pin_1
